# Fritzing sketch fritzing sketch (saved by Fritzing 0.9.5d)

parts:
  U1 = ESP8266 NodeMCU LoLin module
  Part1 = LCD1602-I2C
  Sensor1 = Gas Sensor Breakout Board
  Sensor2 = Gas Sensor Breakout Board
  A1 = DHT22 module
  Part2 = ADS1115

nets:
  N1: U1.D1, Part1.SCL
  N2: U1.D2, Part1.SDA
  3V3: U1.3V3, Part1.VCC, Part2.VDD
  GND: U1.GND, A1.-, Part2.GND
  N3: U1.D5, A1.Out
  N4: Sensor1.AOUT, Part2.A0
  N5: Sensor2.AOUT, Part2.A1

custom parts:
  ESP8266 NodeMCU LoLin module: ESP8266 based NodeMCU
  LCD1602-I2C: A standard character display, usually with 2x16 characters. Comes in many colors with LCM1602 IIC attached.
  Gas Sensor Breakout Board: Gas sensor breakout board. Input voltage is 5V. Sensor output is available in analog and digital.
  DHT22 module: DHT22 module. Pins VCC Data GND.
  ADS1115: ADC ADS1115
